# Fritzing sketch irreceiver (saved by Fritzing 0.9.3b)
breadboards: 1

parts:
  Part1 = Arduino Uno (Rev3) - ICSP
  IR1 = TSOP312.., 314.. [package=THT]

nets:
  N1: Part1.D2, IR1.GND
  N2: Part1.5V, IR1.Data
  N3: Part1.GND, IR1.Vs
