# Fritzing sketch irtransmitter (saved by Fritzing 0.9.3b)
breadboards: 1

parts:
  Part1 = Arduino Uno (Rev3) - ICSP
  S1 = Pushbutton [package="[THT]"]
  LED1 = LED - 5mm [color="Red (633nm)" package="5 mm [THT]"]
  R1 = Resistor [package="2010 [SMD]"]

nets:
  N1: Part1.D10_PWM/SS, S1.Pin_3, S1.Pin_4, R1.Pin_1
  N2: Part1.D13/SCK, LED1.anode
  N3: Part1.5V, S1.Pin_1, S1.Pin_2
  N4: Part1.GND, LED1.cathode, R1.Pin_0

notes:
  (these two are reversed)

custom parts:
  Resistor: Resistor Basic schematic elements and footprints for 0603, 1206, and PTH resistors.
